# Fritzing sketch PCB_For_tarcker-V2.0 (saved by Fritzing 0.9.3b)
circuit board: 3.58971cm x 4.75419cm
breadboards: 1

parts:
  Composant1 = Arduino Pro Mini v13
  U1 = SUP500F [package=sup500f]
  Debugger1 = Debugger
  Mod1 = RYLR896 [package=THT]

nets:
  N1: Composant1.D0/TX, Debugger1.3v
  N2: Composant1.D1/RX, U1.VCC
  N3: Composant1.VCC, Debugger1.RX
  GND: Composant1.GND, U1.RX-I, Debugger1.GND
  N4: Composant1.RAW, Debugger1.TX
  N5: Composant1.D8, Mod1.pin3#2
  N6: Composant1.D7, Mod1.pin3#3
  N7: Composant1.D5_PWM, U1.TX-O
  N8: Composant1.D4, U1.GND

notes:
  GND: Black
  VCC: Red
  RX: Yellow
  TX: Green

custom parts:
  RYLR896: RYLR896 UART Interface 868/915mhz LORA Transceiver Module
